# Fritzing sketch 02-semaforo (saved by Fritzing 0.9.3b)
breadboards: 1

parts:
  WeMos_D1_R1 = WeMos D1 R2
  LED1 = LED - 3mm [color="Red (633nm)" package="3 mm [THT]"]
  LED2 = LED - 3mm [color="Yellow (595nm)" package="3 mm [THT]"]
  LED3 = LED - 3mm [color="Green (560nm)" package="3 mm [THT]"]

nets:
  N1: WeMos_D1_R1.GND, LED1.cathode, LED2.cathode, LED3.cathode
  N2: WeMos_D1_R1.5V, LED1.anode, LED2.anode, LED3.anode

custom parts:
  WeMos D1 R2: The D1 R2 is a mini wifi board based on the ESP-8266EX.
